// Logisim project task.circ as structural Verilog: 1 circuit, main circuit main
module main (
  input  V
);

  wire and_1_out, and_2_out, and_3_out, clock_1_out, T1_q, T1_qn, T2_q, T2_qn, T3_q, T3_qn, T4_q;

  Clock clock_1 (.out(clock_1_out));
  and and_1 (and_1_out, T1_qn, V);
  and and_2 (and_2_out, T2_qn, T1_qn, V);
  and and_3 (and_3_out, T3_qn, T2_qn, T1_qn, V);
  T_Flip_Flop T1 (.T(V), .clk(clock_1_out), .Q(T1_q), .Qn(T1_qn));  // open: reset, preset
  T_Flip_Flop T2 (.T(and_1_out), .clk(clock_1_out), .Q(T2_q), .Qn(T2_qn));  // open: reset, preset
  T_Flip_Flop T3 (.T(and_2_out), .clk(clock_1_out), .Q(T3_q), .Qn(T3_qn));  // open: reset, preset
  T_Flip_Flop T4 (.T(and_3_out), .clk(clock_1_out), .Q(T4_q));  // open: Qn, reset, preset
  // Probe on T1_q
  // Probe on T2_q
  // Probe on T3_q
  // Probe on T4_q
endmodule
